# Fritzing sketch ESP32_radio (saved by Fritzing 0.9.3b)
circuit board: 8.46667cm x 5.64444cm
breadboards: 1

parts:
  SP2 = SPEAKER [package=pcb_mount_speaker]
  VS1053B2 = VS1053B
  AMP1 = GF1002 Stereo Amplifier
  M1 = DOIT Esp32 DevKit v1 (30 pins long, 11 pins width) [part_number=ESP32S-PIN30]
  TFT1 = Color 320x240 TFT Display, ILI9341 Controller Chip
  R1 = Trimmer Potentiometer [maximum_resistance=10kΩ package=THT]
  C1 = Ceramic Capacitor [capacitance=100nF package="100 mil [THT, multilayer]"]
  C2 = Ceramic Capacitor [capacitance=100nF package="100 mil [THT, multilayer]"]
  RE1 = Rotary Encoder [package=THT]
  S1 = Pushbutton [package=THT]
  C3 = Ceramic Capacitor [capacitance=100nF package="100 mil [THT, multilayer]"]
  J1 = male pin header, 5 pins [form="♂ (male)"]
  R6 = Resistor [tolerance=±5% resistance=1k package="0805 [SMD]"]
  R3 = Resistor [tolerance=±5% resistance=10k package="0805 [SMD]"]
  R2 = Resistor [tolerance=±5% resistance=10k package="0805 [SMD]"]
  R8 = Resistor [tolerance=±5% resistance=10k package="0805 [SMD]"]
  R7 = Resistor [tolerance=±5% resistance=10k package="0805 [SMD]"]
  IC1 = Voltage Regulator LM1117 [part_number="AMS1117 3.3V" package=sot223]
  C4 = Electrolytic Capacitor [capacitance=47µF voltage=50V part_number=10-100uF package="100 mil [THT, electrolytic]"]
  C6 = Electrolytic Capacitor [capacitance=22µF part_number="22-47uF 0.3-22 ESR" package="100 mil [THT, electrolytic]"]

nets:
  N1: SP2.+, AMP1.LOUT-
  N2: SP2.-, AMP1.LOUT+
  3.3V: VS1053B2.Vcc, M1.3V3, TFT1.VCC, R1.leg2, J1.pin5, R8.Pin_0, R7.Pin_0, IC1.OUT, C6.+
  GND: VS1053B2.Gnd, M1.GND, TFT1.GND, C1.0, C2.0, RE1.EncoderPinC, S1.leg0, C3.0, J1.pin4, IC1.ADJ, C4.-, C6.-
  N3: VS1053B2.XCS, M1.D32
  N4: VS1053B2.XDCS, M1.D33, TFT1.D/C
  N5: VS1053B2.DREQ, M1.D35
  N6: VS1053B2.MOSI, M1.D23, TFT1.SDI_(MOSI)
  N7: VS1053B2.SCK, M1.D18, TFT1.SCK
  N8: VS1053B2.MISO, M1.D19, TFT1.SDO_(MISO)
  N9: VS1053B2.XRST, M1.EN, TFT1.Reset
  GPIO15: M1.D15, C3.1, R6.Pin_0
  GPIO2: M1.D2, C1.1, R3.Pin_1
  GPIO4: M1.D4, C2.1, R2.Pin_0
  N10: M1.D27, TFT1.CS
  N11: M1.VIN, IC1.IN, C4.+
  N12: TFT1.LED, R1.wiper
  N13: RE1.EncoderPinA, J1.pin2, R3.Pin_0, R8.Pin_1
  N14: RE1.EncoderPinB, J1.pin3, R2.Pin_1, R7.Pin_1
  N15: S1.leg1, J1.pin1, R6.Pin_1

custom parts:
  VS1053B: VS1053B module
  GF1002 Stereo Amplifier: GF1002 6 Watt Stereo Amplifier
  DOIT Esp32 DevKit v1 (30 pins long, 11 pins width): The DOIT Esp32 DevKit v1 is one of the development board created by DOIT to evaluate the ESP-WROOM-32 module. It is based on the ESP32 microcontroller that boasts Wifi, Bluetooth, Ethernet and Low Power support all in a single chip. (vanepp) made breadboard work, adjusted pin numbering and labels and reduced size of schematic and cleaned up pcb. This chip is 30pins long (2 x15) and 11 pins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
  Color 320x240 TFT Display, ILI9341 Controller Chip: 2.2" TFT Display with ILI9341 Controller
